// Logisim project 09counterbubblepushing.circ as structural Verilog: 1 circuit, main circuit main
module main (
  input  w,
  input  x,
  input  y,
  input  z
);

  wire nand_1_out, nand_2_out, nand_3_out, nand_4_out, nand_5_out, nand_6_out, nand_7_out, nand_8_out,
       nand_9_out, nand_10_out, nand_11_out, nand_12_out, nand_13_out, nand_14_out, nand_15_out, nand_16_out,
       nand_17_out, nand_18_out, nand_19_out, nand_20_out, nand_21_out, not_1_out, not_2_out, not_3_out,
       not_4_out;

  not not_1 (not_1_out, w);
  not not_2 (not_2_out, x);
  not not_3 (not_3_out, y);
  not not_4 (not_4_out, z);
  nand nand_1 (nand_1_out, x, y, z);
  nand nand_2 (nand_2_out, not_2_out, not_4_out);
  nand nand_3 (nand_3_out, y, z);
  nand nand_4 (nand_4_out, not_3_out, not_4_out);
  nand nand_5 (nand_5_out, not_3_out, z);
  nand nand_6 (nand_6_out, x, not_3_out, not_4_out);
  nand nand_7 (nand_7_out, not_2_out, y, not_4_out);
  nand nand_8 (nand_8_out, x, z);
  nand nand_9 (nand_9_out, not_2_out, y);
  nand nand_10 (nand_10_out, not_2_out, z);
  nand nand_11 (nand_11_out, x, not_3_out);
  nand nand_12 (nand_12_out, not_1_out, not_3_out, nand_1_out);
  nand nand_13 (nand_13_out, x, nand_3_out, nand_4_out);
  nand nand_14 (nand_14_out, not_1_out, nand_5_out, nand_6_out);
  nand nand_15 (nand_15_out, nand_5_out, nand_8_out);
  nand nand_16 (nand_16_out, not_1_out, nand_3_out, nand_9_out);
  nand nand_17 (nand_17_out, nand_12_out, nand_2_out);
  nand nand_18 (nand_18_out, nand_14_out, nand_7_out, nand_1_out);
  nand nand_19 (nand_19_out, not_1_out, not_2_out, y, not_4_out);
  nand nand_20 (nand_20_out, nand_16_out, nand_10_out);
  nand nand_21 (nand_21_out, not_1_out, nand_5_out, nand_9_out, nand_11_out);
  _7_Segment_Display u_7_segment_display_1 (
    .g(nand_21_out), .f(nand_20_out), .a(nand_17_out), .b(nand_13_out), .e(nand_15_out), .d(nand_18_out),
    .c(nand_19_out));  // open: dp

  // Notes on the sheet:
  //   b = x’ + y’z’+ yz
  //   c = w + x + y’ + z
  //   e = yz’ + x’z’
  //   a = w + y + x’y’z’ + xz
  //   d= w + yz’ + x’yz + x’y’z’ + xy’z
  //   f = w + y’z’ + xy’ + xz’
  //   g = w + yz’ + xy’ + x’y
endmodule
