// Logisim project 09counterdontcares.circ as structural Verilog: 1 circuit, main circuit main
module main (
  input  w,
  input  x,
  input  y,
  input  z
);

  wire a_out, b_out, c_out, d_out, e_out, f_out, g_out, not_1_out, not_2_out, not_3_out, not_4_out,
       nx_ny_nz_out, nx_nz_out, nx_y_out, nx_y_z_out, ny_nz_out, or_1_out, or_2_out, or_3_out, or_4_out,
       or_5_out, x_ny_out, x_ny_z_out, x_nz_out, x_z_out, y_nz_out, y_z_out;

  not not_1 (not_1_out, w);
  not not_2 (not_2_out, x);
  not not_3 (not_3_out, y);
  not not_4 (not_4_out, z);
  and nx_ny_nz (nx_ny_nz_out, not_2_out, not_3_out, not_4_out);
  and x_z (x_z_out, x, z);
  and ny_nz (ny_nz_out, not_3_out, not_4_out);
  and y_z (y_z_out, y, z);
  and y_nz (y_nz_out, y, not_4_out);
  and nx_y_z (nx_y_z_out, not_2_out, y, z);
  and x_ny_z (x_ny_z_out, x, not_3_out, z);
  and nx_nz (nx_nz_out, not_2_out, not_4_out);
  and x_ny (x_ny_out, x, not_3_out);
  and x_nz (x_nz_out, x, not_4_out);
  and nx_y (nx_y_out, not_2_out, y);
  or or_1 (or_1_out, w, y, nx_ny_nz_out);
  or b (b_out, not_2_out, ny_nz_out, y_z_out);
  or or_2 (or_2_out, w, y_nz_out, nx_y_z_out);
  or e (e_out, y_nz_out, nx_nz_out);
  or or_3 (or_3_out, w, x, not_3_out);
  or or_4 (or_4_out, w, ny_nz_out, x_ny_out);
  or or_5 (or_5_out, w, y_nz_out, x_ny_out);
  or a (a_out, or_1_out, x_z_out);
  or d (d_out, or_2_out, x_ny_z_out, nx_ny_nz_out);
  or c (c_out, or_3_out, z);
  or f (f_out, or_4_out, x_nz_out);
  or g (g_out, or_5_out, nx_y_out);
  _7_Segment_Display u_7_segment_display_1 (
    .g(g_out), .f(f_out), .a(a_out), .b(b_out), .e(e_out), .d(d_out), .c(c_out));  // open: dp

  // Notes on the sheet:
  //   a = w + y + x’y’z’ + xz
  //   b = x’ + y’z’+ yz
  //   c = w + x + y’ + z
  //   e = yz’ + x’z’
  //   f = w + y’z’ + xy’ + xz’
  //   g = w + yz’ + xy’ + x’y
  //   d= w + yz’ + x’yz + x’y’z’ + xy’z
endmodule
