// Logisim project Demorgansreducedbubblepushing2gates.circ as structural Verilog: 1 circuit, main circuit main
module main (
  input  w,
  input  x,
  input  y,
  input  z
);

  wire a_out, b_out, c_out, d_out, e_out, f_out, g_out, nand_1_out, nor_1_out, not_1_out, not_2_out,
       not_3_out, not_4_out, nx_ny_nz_out, nx_y_out, nx_y_z_out, ny_nz_out, x_ny_out, x_ny_z_out, x_z_out,
       y_nz_out, y_z_out;

  not not_1 (not_1_out, w);
  not not_2 (not_2_out, x);
  not not_3 (not_3_out, y);
  not not_4 (not_4_out, z);
  nand nx_ny_nz (nx_ny_nz_out, not_2_out, not_3_out, not_4_out);
  nand x_z (x_z_out, x, z);
  nand ny_nz (ny_nz_out, not_3_out, not_4_out);
  nand y_z (y_z_out, y, z);
  nand y_nz (y_nz_out, y, not_4_out);
  nand nx_y_z (nx_y_z_out, not_2_out, y, z);
  nand x_ny_z (x_ny_z_out, x, not_3_out, z);
  nand x_ny (x_ny_out, x, not_3_out);
  nand nx_y (nx_y_out, not_2_out, y);
  nand nand_1 (nand_1_out, y_nz_out, nx_y_z_out, nx_ny_nz_out, x_ny_z_out);
  nand e (e_out, y_nz_out, nx_ny_nz_out);
  nand c (c_out, not_1_out, not_2_out, y, not_4_out);
  nand a (a_out, not_1_out, not_3_out, nx_ny_nz_out, x_z_out);
  nand b (b_out, x, ny_nz_out, y_z_out);
  nor nor_1 (nor_1_out, nand_1_out, nand_1_out);
  nand f (f_out, ny_nz_out, not_1_out, x_ny_out, not_2_out);
  nand g (g_out, not_1_out, y_nz_out, x_ny_out, nx_y_out);
  _7_Segment_Display u_7_segment_display_1 (
    .g(g_out), .f(f_out), .a(a_out), .b(b_out), .e(e_out), .d(d_out), .c(c_out));  // open: dp
  nand d (d_out, not_1_out, nor_1_out);

  // Notes on the sheet:
  //   SOP
  //   a = w + y + x’y’z’ + xz
  //   b = x’ + y’z’+ yz
  //   c = w + x + y’ + z
  //   e = yz’ + x’z’
  //   f = w + y’z’ + xy’ + xz’
  //   g = w + yz’ + xy’ + x’y
  //   d= w + yz’ + x’yz + x’y’z’ + xy’z
  //   b = x’ + y’z’+ yz
  //   c = w + x + y’ + z
  //   e = yz’ + x’z’
  //   Inverse / Bubble Push
  //   a = w + y + x’y’z’ + xz
  //   a' = (w' . y' . (x’y’z’)' . (xz)')'
  //   b' = (x . (y'z')' . (yz)' )'
  //   c= (w' . x' . y . z')'
  //   c= NAND(w',x',y,z')
  //   d= w + yz’ + x’yz + x’y’z’ + xy’z
  //   f = w + y’z’ + xy’ + xz’
  //   g = w + yz’ + xy’ + x’y
  //   a=NAND(w', y', NAND(x',y',z'), NAND(x,z))
  //   b = NAND(x, NAND(y',z'), NAND(y,z) )
  //   e = NAND( NAND(y,z'), NAND(x',z'))
  //   f=NAND( w', NAND(y’,z’), NAND(x,y’), NAND(x,z’)  )
  //   g= NAND( w' . NAND(yz’) . NAND(xy’) . NAND(x’y))
  //   d= NAND( w, NOT(NAND( NAND(yz’), NAND(x’yz), NAND(x’y’z’), NAND(xy’z))))
endmodule
