// Logisim project Faopt.circ as structural Verilog
module FAOpt2 (
  input  a,
  input  b,
  input  cin,
  output sum,
  output cout
);

  wire nand_1_out, nand_2_out, nand_3_out, nand_4_out, nor_1_out, nor_2_out, nor_3_out, not_1_out, not_2_out;

  nor nor_1 (nor_1_out, a, b);
  not not_1 (not_1_out, nand_1_out);
  nand nand_1 (nand_1_out, a, b);
  nor nor_2 (nor_2_out, nor_1_out, not_1_out);
  nor nor_3 (nor_3_out, nor_2_out, cin);
  not not_2 (not_2_out, nand_2_out);
  nand nand_2 (nand_2_out, nor_2_out, cin);
  nand nand_3 (nand_3_out, b, cin);
  nand nand_4 (nand_4_out, a, cin);
  nor nor_4 (sum, nor_3_out, not_2_out);
  nand nand_5 (cout, nand_1_out, nand_3_out, nand_4_out);

  // Notes on the sheet:
  //   FAOpt2
  //   Pranav Maheshwaran
  //   Transistors: 42
  //   5.5 if Cin < 2.75
  //    Cin + 2.25
  //   Cin + 2.75 if Cin > 2.75
endmodule

module FAOpt1 (
  input  a,
  input  b,
  input  cin,
  output sum,
  output carry
);

  wire nand_1_out, nand_2_out, nor_1_out, nor_2_out, nor_3_out, not_1_out, not_2_out;

  nor nor_1 (nor_1_out, a, b);
  not not_1 (not_1_out, nand_1_out);
  nand nand_1 (nand_1_out, a, b);
  nor nor_2 (nor_2_out, nor_1_out, not_1_out);
  nand nand_2 (nand_2_out, nor_2_out, cin);
  nor nor_3 (nor_3_out, nor_2_out, cin);
  not not_2 (not_2_out, nand_2_out);
  nor nor_4 (sum, nor_3_out, not_2_out);
  nand nand_3 (carry, nand_2_out, nand_1_out);

  // Notes on the sheet:
  //   FAopt1
  //   Pranav Maheshwaran
  //   32 Transistors
  //   Delay to Cout
  //   Cin + 2.75
  //   Both are 2.5, use Faopt1 & FAopt 2
  //   5.5, Cin < 2.75
  //   Cin +2.75, Cin > 2.75
  //   4.75, Cin < 2.75
  //   Cin +2, Cin > 2.75
endmodule

module adder4bit (
  input  [3:0] a,
  input  [3:0] b,
  input  cin,
  output [3:0] out_4,
  output cout
);

  wire faopt1_2_carry, faopt1_3_carry, faopt1_4_carry;

  FAOpt1 faopt1_1 (.b(b[3]), .cin(faopt1_2_carry), .a(a[3]), .sum(out_4[3]), .carry(cout));
  FAOpt1 faopt1_2 (.b(b[2]), .cin(faopt1_3_carry), .a(a[2]), .sum(out_4[2]), .carry(faopt1_2_carry));
  FAOpt1 faopt1_3 (.b(b[1]), .cin(faopt1_4_carry), .a(a[1]), .sum(out_4[1]), .carry(faopt1_3_carry));
  FAOpt1 faopt1_4 (.b(b[0]), .cin(cin), .a(a[0]), .sum(out_4[0]), .carry(faopt1_4_carry));

  // Notes on the sheet:
  //   10.75
  //   8.75
  //   11.5
  //   9.5
  //   6.75
  //   4.75
  //   7.5
  //   4.75
endmodule

module HA1 (
  input  a,
  input  b,
  output Sum,
  output Carry
);

  wire nor_1_out;

  nor nor_1 (nor_1_out, a, b);
  and and_1 (Carry, b, a);
  nor nor_2 (Sum, nor_1_out, Carry);
endmodule

module CSA1 (
  input  [7:0] a,
  input  [7:0] b,
  input  cin,
  output [7:0] sum,
  output overflow
);

  wire adder4bit_1_cout, adder4bit_2_cout, adder4bit_3_cout;
  wire [3:0] adder4bit_2_out_4, adder4bit_3_out_4;

  adder4bit adder4bit_1 (.a(a[3:0]), .b(b[3:0]), .cin(cin), .out_4(sum[3:0]), .cout(adder4bit_1_cout));
  adder4bit adder4bit_2 (.a(a[7:4]), .b(b[7:4]), .cin(1'b1), .out_4(adder4bit_2_out_4), .cout(adder4bit_2_cout));
  mx2i_4 mx2i_4_1 (.in1(adder4bit_2_out_4), .in0(adder4bit_3_out_4), .s(adder4bit_1_cout), .out_4(sum[7:4]));
  adder4bit adder4bit_3 (.a(a[7:4]), .b(b[7:4]), .cin(1'b0), .out_4(adder4bit_3_out_4), .cout(adder4bit_3_cout));
  Mux_main main_1 (.a(adder4bit_3_cout), .s(adder4bit_1_cout), .b(adder4bit_2_cout), .out_4(overflow));

  // Notes on the sheet:
  //   c4
  //   10.75
  //   10.75
  //   11.5
  //   cout1
  //   10.75
  //   sum1
  //   11.5
  //   cout0
  //   sum0
  //   11.5
  //   15.0
  //   15.0
endmodule

module CSA2NoCarry (
  input  [15:0] a,
  input  [15:0] b,
  input  cin,
  output [15:0] sum,
  output overflow
);

  wire csa1_1_overflow, csa1_2_overflow, csa1_3_overflow;
  wire [7:0] csa1_2_sum, csa1_3_sum;

  CSA1 csa1_1 (.a(a[7:0]), .b(b[7:0]), .cin(cin), .sum(sum[7:0]), .overflow(csa1_1_overflow));
  CSA1 csa1_2 (.a(a[15:8]), .b(b[15:8]), .cin(1'b1), .sum(csa1_2_sum), .overflow(csa1_2_overflow));
  CSA1 csa1_3 (.a(a[15:8]), .b(b[15:8]), .cin(1'b0), .sum(csa1_3_sum), .overflow(csa1_3_overflow));
  mx2i_8 mx2i_8_1 (.s(csa1_1_overflow), .in0(csa1_3_sum), .in1(csa1_2_sum), .out_4(sum[15:8]));
  Mux_main main_1 (.a(csa1_3_overflow), .s(csa1_1_overflow), .b(csa1_2_overflow), .out_4(overflow));

  // Notes on the sheet:
  //   c4
  //   13.25
  //   cout1
  //   12.75
  //   sum1
  //   13.25
  //   cout0
  //   12.75
  //   sum0
  //   13.25
  //   17.5
  //   17.00
endmodule

module CSA2 (
  input  [15:0] a,
  input  [15:0] b,
  input  cin,
  output [15:0] sum,
  output overflow
);

  wire csa1_1_overflow, csa1_2_overflow, csa1_3_overflow;
  wire [7:0] csa1_2_sum, csa1_3_sum;

  CSA1 csa1_1 (.a(a[7:0]), .b(b[7:0]), .cin(cin), .sum(sum[7:0]), .overflow(csa1_1_overflow));
  CSA1 csa1_2 (.a(a[15:8]), .b(b[15:8]), .cin(cin), .sum(csa1_2_sum), .overflow(csa1_2_overflow));
  CSA1 csa1_3 (.a(a[15:8]), .b(b[15:8]), .cin(1'b0), .sum(csa1_3_sum), .overflow(csa1_3_overflow));
  mx2i_8 mx2i_8_1 (.s(csa1_1_overflow), .in0(csa1_3_sum), .in1(csa1_2_sum), .out_4(sum[15:8]));
  Mux_main main_1 (.a(csa1_3_overflow), .s(csa1_1_overflow), .b(csa1_2_overflow), .out_4(overflow));

  // Notes on the sheet:
  //   c4
  //   cout1
  //   15.0
  //   15.0
  //   cout0
  //   15.0
  //   sum1
  //   15.0
  //   sum0
  //   15.0
  //   19.25
  //   19.25
endmodule

module mx2i_4 (
  input  [3:0] in0,
  input  [3:0] in1,
  input  s,
  output [3:0] out_4
);

  Mux_main main_1 (.a(in0[0]), .s(s), .b(in1[0]), .out_4(out_4[0]));
  Mux_main main_2 (.a(in0[1]), .s(s), .b(in1[1]), .out_4(out_4[1]));
  Mux_main main_3 (.a(in0[2]), .s(s), .b(in1[2]), .out_4(out_4[2]));
  Mux_main main_4 (.a(in0[3]), .s(s), .b(in1[3]), .out_4(out_4[3]));
endmodule

module mx2i_8 (
  input  [7:0] in0,
  input  [7:0] in1,
  input  s,
  output [7:0] out_4
);

  mx2i_4 mx2i_4_1 (.in1(in1[3:0]), .in0(in0[3:0]), .s(s), .out_4(out_4[3:0]));
  mx2i_4 mx2i_4_2 (.in1(in1[7:4]), .in0(in0[7:4]), .s(s), .out_4(out_4[7:4]));
endmodule

module addersubract16bit (
  input  op,
  input  [15:0] A,
  input  [15:0] B,
  output [15:0] sum,
  output overflow
);

  wire adder_1_cout, and_1_out, and_2_out, and_3_out, and_4_out, and_5_out, and_6_out, not_2_out, not_3_out,
       not_4_out, not_5_out, not_6_out, not_7_out, or_1_out, or_2_out, or_3_out, ov_add_out, ov_sub_out;
  wire [15:0] multiplexer_1_out, not_1_out;

  assign not_1_out = ~B;  // NOT_Gate not_1, 16 bits wide
  Adder #(.width(16)) adder_1 (.a(A), .b(multiplexer_1_out), .out(sum), .cin(op), .cout(adder_1_cout));
  Multiplexer #(.width(16)) multiplexer_1 (.in0(B), .in1(not_1_out), .out(multiplexer_1_out), .sel(op));
  not not_2 (not_2_out, A[15]);
  not not_3 (not_3_out, B[15]);
  not not_4 (not_4_out, B[15]);
  not not_5 (not_5_out, A[15]);
  not not_6 (not_6_out, A[15]);
  not not_7 (not_7_out, sum[15]);
  and and_1 (and_1_out, A[15], B[15]);
  and and_2 (and_2_out, not_2_out, not_3_out);
  and and_3 (and_3_out, A[15], not_4_out);
  and and_4 (and_4_out, not_5_out, B[15]);
  and and_5 (and_5_out, sum[15], not_6_out);
  and and_6 (and_6_out, not_7_out, A[15]);
  or or_1 (or_1_out, and_1_out, and_2_out);
  or or_2 (or_2_out, and_3_out, and_4_out);
  or or_3 (or_3_out, and_5_out, and_6_out);
  and ov_add (ov_add_out, or_1_out, or_3_out);
  and ov_sub (ov_sub_out, or_2_out, or_3_out);
  Multiplexer multiplexer_2 (.in0(ov_add_out), .in1(ov_sub_out), .out(overflow), .sel(op));

  // Notes on the sheet:
  //   1 is subtraction, 0 is addition
  //   sa
  //   sb
  //   ss
  //   sa
  //   sb
  //   ss
  //   sa==sb
  //   sa !=sb
  //   ss !=sa
endmodule

module csa_addersubtract16bit (
  input  op,
  input  [15:0] A,
  input  [15:0] B,
  output [15:0] sum,
  output overflow
);

  wire and_1_out, and_2_out, and_3_out, and_4_out, and_5_out, and_6_out, not_2_out, not_3_out, not_4_out,
       not_5_out, not_6_out, not_7_out, or_1_out, or_2_out, or_3_out, ov_add_out, ov_sub_out;
  wire [15:0] multiplexer_1_out, not_1_out;

  assign not_1_out = ~B;  // NOT_Gate not_1, 16 bits wide
  Multiplexer #(.width(16)) multiplexer_1 (.in0(B), .in1(not_1_out), .out(multiplexer_1_out), .sel(op));
  CSA2 csa2_1 (.a(A), .b(multiplexer_1_out), .cin(op), .sum(sum));  // open: overflow
  not not_2 (not_2_out, A[15]);
  not not_3 (not_3_out, B[15]);
  not not_4 (not_4_out, B[15]);
  not not_5 (not_5_out, A[15]);
  not not_6 (not_6_out, A[15]);
  not not_7 (not_7_out, sum[15]);
  and and_1 (and_1_out, A[15], B[15]);
  and and_2 (and_2_out, not_2_out, not_3_out);
  and and_3 (and_3_out, A[15], not_4_out);
  and and_4 (and_4_out, not_5_out, B[15]);
  and and_5 (and_5_out, sum[15], not_6_out);
  and and_6 (and_6_out, not_7_out, A[15]);
  or or_1 (or_1_out, and_1_out, and_2_out);
  or or_2 (or_2_out, and_3_out, and_4_out);
  or or_3 (or_3_out, and_5_out, and_6_out);
  and ov_add (ov_add_out, or_1_out, or_3_out);
  and ov_sub (ov_sub_out, or_2_out, or_3_out);
  Multiplexer multiplexer_2 (.in0(ov_add_out), .in1(ov_sub_out), .out(overflow), .sel(op));

  // Notes on the sheet:
  //   1 is subtraction, 0 is addition
  //   sa
  //   sb
  //   select logic
  //   ss
  //   sa
  //   sb
  //   ss
  //   sa==sb
  //   sa !=sb
  //   ss !=sa
  //   overflow logic
endmodule

module cla1 (
  input  P3,
  input  P2,
  input  P1,
  input  P0,
  input  G3,
  input  G2,
  input  G1,
  input  G0,
  input  C0,
  output out_10
);

  wire T2_out, T3_out, T4_out, T5_out;

  and T2 (T2_out, P3, G2);
  and T3 (T3_out, P3, G1, P2);
  and T4 (T4_out, P3, P2, P1, G0);
  and T5 (T5_out, P3, P2, P1, P0, C0);
  or C4 (out_10, T2_out, T3_out, T4_out, T5_out, G3);
endmodule
