// Logisim project Mux.circ as structural Verilog: 3 circuits, main circuit main
module main (
  input  a,
  input  s,
  input  b,
  output out_4
);

  wire nand_1_out, nand_2_out, not_1_out;

  not not_1 (not_1_out, s);
  nand nand_1 (nand_1_out, a, not_1_out);
  nand nand_2 (nand_2_out, b, s);
  nand nand_3 (out_4, nand_1_out, nand_2_out);

  // Notes on the sheet:
  //   2 to 1 MUX
  //   Pranav Maheshwaran
  //   z = max(s+2.75, in0+2.5, in1+2.5)
endmodule

module Mux4 (
  input  d0,
  input  d1,
  input  s1,
  input  s2,
  input  d2,
  input  d3,
  output out_7
);

  wire main_1_out_4, main_2_out_4;

  main main_1 (.a(d0), .s(s1), .b(d1), .out_4(main_1_out_4));
  main main_2 (.a(d2), .s(s1), .b(d3), .out_4(main_2_out_4));
  main main_3 (.a(main_1_out_4), .s(s2), .b(main_2_out_4), .out_4(out_7));

  // Notes on the sheet:
  //   4-to-1 Multiplexer
  //   Pranav Maheshwaran
  //   z = max(s0+2.75, s1+2.75, in0+5, in1+5, in2+5, in3+5) 
endmodule

module transmission_2mux (
  input  in0,
  input  in1,
  input  sel,
  output out_4
);

  wire transmission_1_p3, transmission_1_p4;

  // Transmission_Gate transmission_1: pin names not known; wires that end beside it: in0, sel, transmission_1_p3, transmission_1_p4
  not not_1 (transmission_1_p3, sel);
  // Transmission_Gate transmission_2: pin names not known; wires that end beside it: in1, transmission_1_p3, sel, transmission_1_p4
  not not_2 (out_4, transmission_1_p4);

  // Notes on the sheet:
  //   z = max(s+1, in0+0.25, in1+0.25)
endmodule
