// Logisim project anode_cir_pranav_formula_1.circ as structural Verilog: 1 circuit, main circuit main
module main (
  input  w2,
  input  x2,
  input  y2,
  input  z2,
  input  w,
  input  x,
  input  y,
  input  z,
  input  w1,
  input  x1,
  input  y1,
  input  z1
);

  wire a1_out, a2_out, a_out, b1_out, b2_out, b_out, c1_out, c2_out, d1_out, d2_out, d_out, e1_out, e2_out,
       e_out, f1_out, f2_out, f_out, g1_out, g2_out, g_out, n_ny_nz_out, nand_1_out, nand_2_out, nand_3_out,
       nand_4_out, nand_5_out, nand_6_out, nand_7_out, nand_8_out, nand_9_out, nand_10_out, nand_11_out,
       nand_12_out, nand_13_out, nand_14_out, nand_15_out, nand_16_out, nand_17_out, nand_18_out,
       nand_19_out, nand_20_out, not_1_out, not_2_out, not_3_out, not_4_out, not_5_out, not_6_out, not_7_out,
       not_8_out, not_9_out, not_10_out, not_11_out, not_12_out, nw_nx_ny_out, nw_nx_ny_z_out, nw_nx_y_out,
       nw_nx_z_out, nx_y_nz_out, x_ny_nz_out, x_ny_out, x_ny_z_out, x_y_nz_out, x_y_z_out, y_z_out;

  not not_1 (not_1_out, w);
  not not_2 (not_2_out, x);
  not not_3 (not_3_out, y);
  not not_4 (not_4_out, z);
  and nw_nx_ny_z (nw_nx_ny_z_out, not_1_out, not_2_out, not_3_out, z);
  and x_ny_z (x_ny_z_out, x, not_3_out, z);
  and x_y_nz (x_y_nz_out, x, y, not_4_out);
  and nx_y_nz (nx_y_nz_out, not_2_out, y, not_4_out);
  and n_ny_nz (n_ny_nz_out, x, not_3_out, not_4_out);
  and x_y_z (x_y_z_out, x, y, z);
  and x_ny (x_ny_out, x, not_3_out);
  and y_z (y_z_out, y, z);
  and nw_nx_y (nw_nx_y_out, not_2_out, not_1_out, y);
  and nw_nx_z (nw_nx_z_out, not_1_out, not_2_out, z);
  and nw_nx_ny (nw_nx_ny_out, not_1_out, not_2_out, not_3_out);
  and x_ny_nz (x_ny_nz_out, x, not_3_out, not_4_out);
  or a (a_out, x_ny_nz_out, nw_nx_ny_z_out);
  or b (b_out, x_ny_z_out, x_y_nz_out);
  or d (d_out, n_ny_nz_out, x_y_z_out, nw_nx_ny_z_out);
  or e (e_out, x_ny_out, z);
  or f (f_out, y_z_out, nw_nx_y_out, nw_nx_z_out);
  or g (g_out, nw_nx_ny_out, x_y_z_out);
  _7_Segment_Display #(.active("false")) u_7_segment_display_1 (
    .g(g_out), .f(f_out), .a(a_out), .b(b_out), .e(e_out), .d(d_out), .c(nx_y_nz_out));  // open: dp
  not not_5 (not_5_out, w1);
  not not_6 (not_6_out, x1);
  not not_7 (not_7_out, y1);
  not not_8 (not_8_out, z1);
  nand nand_1 (nand_1_out, x1, not_7_out, not_8_out);
  nand nand_2 (nand_2_out, not_5_out, not_6_out, not_7_out, z1);
  nand nand_3 (nand_3_out, x1, not_7_out, z1);
  nand nand_4 (nand_4_out, x1, y1, not_8_out);
  nor c1 (c1_out, x1, not_7_out, z1);
  nand nand_5 (nand_5_out, x1, not_7_out, not_8_out);
  nand nand_6 (nand_6_out, x1, y1, z1);
  nand nand_7 (nand_7_out, x1, not_7_out);
  nand nand_8 (nand_8_out, y1, z1);
  nand nand_9 (nand_9_out, not_6_out, not_5_out, y1);
  nand nand_10 (nand_10_out, not_5_out, not_6_out, z1);
  nand nand_11 (nand_11_out, not_5_out, not_6_out, not_7_out);
  nand a1 (a1_out, nand_1_out, nand_2_out);
  nand b1 (b1_out, nand_3_out, nand_4_out);
  nand d1 (d1_out, nand_5_out, nand_6_out, nand_2_out);
  nand e1 (e1_out, nand_7_out, not_8_out);
  nand f1 (f1_out, nand_8_out, nand_9_out, nand_10_out);
  nand g1 (g1_out, nand_11_out, nand_6_out);
  _7_Segment_Display #(.active("false")) u_7_segment_display_2 (
    .g(g1_out), .f(f1_out), .a(a1_out), .b(b1_out), .e(e1_out), .d(d1_out), .c(c1_out));  // open: dp
  not not_9 (not_9_out, w2);
  not not_10 (not_10_out, x2);
  not not_11 (not_11_out, y2);
  not not_12 (not_12_out, z2);
  nand nand_12 (nand_12_out, not_9_out, not_10_out, not_11_out, z2);
  nand nand_13 (nand_13_out, x2, not_11_out, not_12_out);
  nand nand_14 (nand_14_out, x2, not_11_out, z2);
  nand nand_15 (nand_15_out, x2, y2, not_12_out);
  nor c2 (c2_out, x2, not_11_out, z2);
  nand nand_16 (nand_16_out, x2, not_11_out, not_12_out);
  nand nand_17 (nand_17_out, x2, y2, z2);
  nand nand_18 (nand_18_out, y2, z2);
  nand nand_19 (nand_19_out, not_9_out, not_10_out, y2);
  nand nand_20 (nand_20_out, not_9_out, not_10_out, not_11_out);
  nand a2 (a2_out, nand_13_out, nand_12_out);
  nand b2 (b2_out, nand_14_out, nand_15_out);
  nand d2 (d2_out, nand_16_out, nand_17_out, nand_12_out);
  nand f2 (f2_out, nand_18_out, nand_12_out, nand_19_out);
  nand g2 (g2_out, nand_20_out, nand_17_out);
  nand e2 (e2_out, nand_13_out, not_12_out);
  _7_Segment_Display #(.active("false")) u_7_segment_display_3 (
    .g(g2_out), .f(f2_out), .a(a2_out), .b(b2_out), .e(e2_out), .d(d2_out), .c(c2_out));  // open: dp

  // Notes on the sheet:
  //   Using Common Anode - Changed 7-Segment Active on High to 0 
  //   c
  //   a = xy’z’+w’x’y’z | b = xy’z+xyz’ | c = x’yz’ | d = xy’z’+xyz+w’x’y’z |  e = z + xy’ | f = yz+w’x’y+w’x’z | g = w’x’y’+xyz
  //   2. Bubble push
  //   Eliminating a Gate in F formula
  //   f = [ (y.z)' . (w'.x'.y)' . (w' . x' . z)' ]'
  //   Using 11D i.e AB' +B = A+B
  //   Let B = (y.z) , A = (w'.x'.z)
  //   Hence the gate (w'.x'.z) in F signal will be eliminated
  //   3. Eliminate two gates 
  //   f = [ (y.z) + (w'.x'.y) + (w' . x' . z) ] , applied DeMorgan's once
  //   f = [  (w'.x'.z . y') + ( w'.x'.z.z') + (y.z) + (w' . x' . y) ]  , Distributing y' and z'
  //   f = [  (w'.x'. y' . z)' . (y.z) . (w' . x' . y)' ]', applied DeMorgans again
  //   f = [  (w'.x'.z) . (y.z)' + (y.z) + (w' . x' . y) ] - applied rule 11D, substitued A and B values
  //   f = [  (w'.x'.z) . (y'+z') + (y.z) + (w' . x' . y) ]  , Expand (y.z)' with DeMorgans becomes y' + z'
  //   a = xy’z’+w’x’y’z | b = xy’z+xyz’ | c = x’yz’ | d = xy’z’+xyz+w’x’y’z |  e = z + xy’ | f = yz+w’x’y+w’x’z | g = w’x’y’+xyz
  //   f = [  (w'.x'.z . y') + 0 + (y.z) + (w' . x' . y) ]  , ( w'.x'.z.z') becomes 0, because z . z' = 0 as per rule 5D
  //   f = [  (w'.x'. y' . z) + (y.z) + (w' . x' . y) ], noticed - term ( w'.x'.y.z') is in A signal formula, we will reuse that
  //   e=[ (x.y')' . z']'
  //   = [x.y'z' + z]
  //   Eliminating a Gate in E formula
  //   Apply De-Morgan once = [ (x.y') + z]
  //   Using 11D i.e AB' +B = A+B
  //   A ==> (x.y'), B==> z
  //   = [x.y'z' + z]'' ==> Apply DeMorgans
  //   = [ (x.y'z')' . z' ]' ==> Apply DeMorgans
  //   [(x.y')+z] = [(x.y') . z' + z], by Substituting A with (x.y') and B with z
  //   (x.y'z') is a gate in A formula, which can be reused and  eliminate the gate in E
endmodule
