// Logisim project cla.circ as structural Verilog: 4 circuits, main circuit main
module main (
  input  p3,
  input  p2,
  input  p1,
  input  p0,
  input  g3,
  input  g2,
  input  g1,
  input  g0,
  input  c0,
  output o1
);

  wire a1_out, a2_out, a3_out, a4_out, n8_out, n9_out, not_1_out, not_2_out, not_3_out, not_4_out, not_5_out,
       not_6_out, not_7_out, t1_out, t2_out, t3_out;

  nand t1 (t1_out, p3, p2);
  not not_1 (not_1_out, t1_out);
  nand t2 (t2_out, not_1_out, p1);
  not not_2 (not_2_out, t2_out);
  nand t3 (t3_out, not_2_out, p0);
  not not_3 (not_3_out, t3_out);
  nand a1 (a1_out, p3, g2);
  not not_4 (not_4_out, a1_out);
  nand a2 (a2_out, not_1_out, g1);
  not not_5 (not_5_out, a2_out);
  nand a3 (a3_out, not_2_out, g0);
  not not_6 (not_6_out, a3_out);
  nand a4 (a4_out, c0, not_3_out);
  not not_7 (not_7_out, a4_out);
  nand n8 (n8_out, g3, not_4_out, not_5_out);
  nand n9 (n9_out, not_6_out, not_7_out);
  nand c4 (o1, n8_out, n9_out);

  // Notes on the sheet:
  //   C0-a4-inv-n9-inv-c4-o1 is the WORST path it could take
endmodule

module cla_c4_3 (
  input  p3,
  input  p2,
  input  p1,
  input  p0,
  input  g3,
  input  g2,
  input  g1,
  input  g0,
  input  c0,
  output out_10
);

  wire a1_out, a2_out, a3_out, and_1_out, nand_1_out, not_1_out, not_2_out, not_3_out, not_4_out, not_5_out,
       not_6_out, not_7_out, not_8_out, or_1_out, t1_out, t2_out, x_out, y_out;

  nand t1 (t1_out, p3, p2);
  not not_1 (not_1_out, t1_out);
  nand a1 (a1_out, p3, g2);
  not not_2 (not_2_out, a1_out);
  nand a2 (a2_out, not_1_out, g1);
  not not_3 (not_3_out, a2_out);
  nand a3 (a3_out, not_5_out, g0);
  not not_4 (not_4_out, a3_out);
  nand t2 (t2_out, not_1_out, p1);
  not not_5 (not_5_out, t2_out);
  nand y (y_out, not_5_out, p0);
  nand nand_1 (nand_1_out, g3, not_2_out, not_3_out);
  not not_6 (not_6_out, y_out);
  nand x (x_out, nand_1_out, not_4_out);
  not not_7 (not_7_out, x_out);
  and and_1 (and_1_out, not_6_out, c0);
  or or_1 (or_1_out, and_1_out, not_7_out);
  not not_8 (not_8_out, or_1_out);
  not not_9 (out_10, not_8_out);
endmodule

module cla_c4_4 (
  input  p3,
  input  p2,
  input  p1,
  input  p0,
  input  g3,
  input  g2,
  input  g1,
  input  g0,
  input  c0,
  output out_10
);

  wire a1_out, a2_out, a3_out, nand_1_out, not_1_out, not_2_out, not_3_out, not_4_out, not_5_out, not_6_out,
       not_7_out, not_8_out, t1_out, t2_out, transistor_1_out, transistor_3_out, transistor_5_out,
       transistor_6_out, x_out, y_out;

  nand t1 (t1_out, p3, p2);
  not not_1 (not_1_out, t1_out);
  nand a1 (a1_out, p3, g2);
  not not_2 (not_2_out, a1_out);
  nand a2 (a2_out, not_1_out, g1);
  not not_3 (not_3_out, a2_out);
  nand a3 (a3_out, not_5_out, g0);
  not not_4 (not_4_out, a3_out);
  nand t2 (t2_out, not_1_out, p1);
  not not_5 (not_5_out, t2_out);
  nand y (y_out, not_5_out, p0);
  nand nand_1 (nand_1_out, g3, not_2_out, not_3_out);
  not not_6 (not_6_out, y_out);
  nand x (x_out, nand_1_out, not_4_out);
  not not_7 (not_7_out, x_out);
  Transistor transistor_1 (.in(transistor_3_out), .out(transistor_1_out), .gate(c0));
  Transistor transistor_2 (.in(transistor_3_out), .out(transistor_1_out), .gate(not_7_out));
  Transistor transistor_3 (.in(not_7_out), .out(transistor_3_out), .gate(not_6_out));
  Transistor #(.\type ("n")) transistor_4 (.in(transistor_6_out), .out(not_7_out), .gate(not_6_out));
  Transistor #(.\type ("n")) transistor_5 (.in(not_7_out), .out(transistor_5_out), .gate(c0));
  Transistor #(.\type ("n")) transistor_6 (.in(transistor_5_out), .out(transistor_6_out), .gate(not_7_out));
  not not_8 (not_8_out, not_7_out);
  not not_9 (out_10, not_8_out);
  // also tied to GND on the sheet: transistor_6_out
  // also tied to VCC on the sheet: transistor_1_out

  // Notes on the sheet:
  //   Fast Carry Path: C0 - AOI21 - inv - c4
  //   Worst Carry Path: p - t1 - t2 - a3 - or - AOI21 - inv - c4
  //   AOI21
endmodule

module test (
  input  g3,
  input  g2,
  input  g1,
  input  g0,
  input  p3,
  input  p2,
  input  p1,
  input  p0,
  input  c0,
  output O0
);

  wire nand_1_out, nand_2_out, nand_3_out, nand_4_out, nand_5_out, nand_6_out, nand_7_out, nand_8_out,
       nand_9_out, nor_1_out, nor_2_out, nor_3_out, nor_4_out, not_1_out, not_3_out, not_4_out, not_5_out,
       not_6_out, not_7_out, not_9_out, not_10_out, not_11_out, not_12_out;

  nand nand_1 (nand_1_out, g2, p3);
  // NAND_Gate nand_2 has open pins: out=nand_2_out
  not not_1 (not_1_out, nand_1_out);
  nand nand_3 (nand_3_out, p3, p2, g1);
  nand nand_4 (nand_4_out, p3, p2);
  nand nand_5 (nand_5_out, p1, g0);
  nand nand_6 (nand_6_out, p3, p2, p1);
  nand nand_7 (nand_7_out, p0, c0);
  // NOT_Gate not_2 has open pins: in=nand_2_out, out=open
  not not_3 (not_3_out, nand_3_out);
  not not_4 (not_4_out, nand_4_out);
  not not_5 (not_5_out, nand_5_out);
  not not_6 (not_6_out, nand_6_out);
  not not_7 (not_7_out, nand_7_out);
  // NOR_Gate nor_1 has open pins: out=nor_1_out
  // NOT_Gate not_8 has open pins: in=nor_1_out, out=open
  nor nor_2 (nor_2_out, not_1_out, not_3_out);
  nand nand_8 (nand_8_out, not_4_out, not_5_out);
  not not_9 (not_9_out, nand_8_out);
  not not_10 (not_10_out, nor_2_out);
  nor nor_3 (nor_3_out, not_10_out, not_9_out);
  nor nor_4 (nor_4_out, not_6_out, not_7_out);
  not not_11 (not_11_out, nor_3_out);
  not not_12 (not_12_out, nor_4_out);
  nand nand_9 (nand_9_out, not_11_out, g3, not_12_out);
  not not_13 (O0, nand_9_out);
endmodule
