// Logisim project lasacs.circ as structural Verilog: 1 circuit, main circuit main
module main (
  input  x,
  input  y,
  input  z
);

  wire a000_out, a001_out, a010_out, a011_out, a100_out, a101_out, a_out, b_out, cg_out, d_out, e_out,
       not_1_out, not_2_out, not_3_out;

  not not_1 (not_1_out, z);
  not not_2 (not_2_out, y);
  not not_3 (not_3_out, x);
  and a000 (a000_out, not_1_out, not_2_out, not_3_out);
  and a001 (a001_out, not_1_out, not_2_out, x);
  and a010 (a010_out, not_1_out, y, not_3_out);
  and a011 (a011_out, not_1_out, y, x);
  and a100 (a100_out, z, not_2_out, not_3_out);
  and a101 (a101_out, z, not_2_out, x);
  or a (a_out, a001_out, a010_out, a011_out, a100_out, a101_out);
  or b (b_out, a001_out, a011_out);
  or cg (cg_out, a001_out, a010_out, a011_out, a101_out);
  or d (d_out, a000_out, a010_out, a100_out, a101_out);
  or e (e_out, a000_out, a001_out, a011_out, a100_out);
  _7_Segment_Display u_7_segment_display_1 (
    .g(cg_out), .f(1'b1), .a(a_out), .b(b_out), .e(e_out), .d(d_out), .c(cg_out));  // open: dp
endmodule
