// Logisim project lasacs_demorgans.circ as structural Verilog: 1 circuit, main circuit main
module main (
  input  z,
  input  y,
  input  x
);

  wire nand_1_out, nand_2_out, nand_3_out, nand_4_out, nor_1_out, nor_2_out, nor_3_out, nor_4_out, not_1_out,
       not_2_out, not_3_out, not_4_out, not_5_out, not_6_out, not_7_out, not_8_out;

  not not_1 (not_1_out, z);
  not not_2 (not_2_out, y);
  not not_3 (not_3_out, x);
  nor nor_1 (nor_1_out, z, x, y);
  nor nor_2 (nor_2_out, z, not_3_out);
  nor nor_3 (nor_3_out, y, x);
  nor nor_4 (nor_4_out, y, x);
  not not_4 (not_4_out, nor_2_out);
  nand nand_1 (nand_1_out, not_1_out, x);
  nand nand_2 (nand_2_out, not_2_out, not_3_out);
  not not_5 (not_5_out, nor_3_out);
  _7_Segment_Display u_7_segment_display_1 (
    .g(not_5_out), .f(1'b1), .a(not_6_out), .b(not_8_out), .e(nand_4_out), .d(not_4_out), .c(not_7_out));  // open: dp
  not not_6 (not_6_out, nor_1_out);
  nand nand_3 (nand_3_out, not_1_out, x);
  not not_7 (not_7_out, nor_4_out);
  not not_8 (not_8_out, nand_3_out);
  nand nand_4 (nand_4_out, nand_1_out, nand_2_out);
endmodule
