// Logisim project lasacs_smplfd.circ as structural Verilog: 1 circuit, main circuit main
module main (
  input  z,
  input  y,
  input  x
);

  wire and_1_out, and_2_out, and_3_out, not_1_out, not_2_out, not_3_out, not_4_out, not_5_out, or_1_out,
       or_2_out, or_3_out, or_4_out;

  not not_1 (not_1_out, z);
  not not_2 (not_2_out, x);
  or or_1 (or_1_out, z, y, x);
  or or_2 (or_2_out, z, not_2_out);
  and and_1 (and_1_out, not_1_out, x);
  not not_3 (not_3_out, z);
  not not_4 (not_4_out, y);
  not not_5 (not_5_out, x);
  or or_3 (or_3_out, y, x);
  and and_2 (and_2_out, not_3_out, x);
  and and_3 (and_3_out, not_4_out, not_5_out);
  _7_Segment_Display u_7_segment_display_1 (
    .g(or_3_out), .f(1'b1), .a(or_1_out), .b(and_1_out), .e(or_4_out), .d(or_2_out), .c(or_3_out));  // open: dp
  or or_4 (or_4_out, and_2_out, and_3_out);
endmodule
